# Fritzing sketch Prototype Schematics (saved by Fritzing 1.0.5)
breadboards: 1

parts:
  Part1 = Arduino Uno (Rev3) - ICSP
  U1 = POT [knob_status=50% power=0.5W package=pot_alpha_rv16af-20]
  S1 = Pushbutton [package="[THT]"]
  U2 = POT [knob_status=50% power=0.5W package=pot_alpha_rv16af-20]
  U3 = POT [knob_status=50% power=0.5W package=pot_alpha_rv16af-20]
  U4 = POT [knob_status=50% power=0.5W package=pot_alpha_rv16af-20]
  Part2 = Arduino Uno (Rev3) - ICSP  # not connected
  U5 = POT [knob_status=50% power=0.5W package=pot_alpha_rv16af-20]  # not connected

nets:
  N1: Part1.A0, U3.S
  N2: Part1.A1, U2.S
  N3: Part1.A2, U1.S
  N4: Part1.A3, U4.S
  N5: Part1.5V, U1.A, U2.A, U3.A, U4.A
  N6: Part1.GND, U1.E, S1.Pin_1, S1.Pin_2, U2.E, U3.E, U4.E
  N7: Part1.D13/SCK, S1.Pin_3, S1.Pin_4
