# Fritzing sketch Robot Arm Schematic (saved by Fritzing 1.0.5)

parts:
  Part1 = 16-Channel 12-bit PWM Servo Driver - I2C [part_number=815]
  A1 = ESP32 DevKitc V4
  J1 = Basic Servo
  J2 = Basic Servo
  J3 = Basic Servo
  J5 = Basic Servo
  M1 = RioRand LM2596
  S1 = Toggle Switch [package=THT]
  JACK1 = 2.1mm Barrel Jack with Terminal Block
  J4 = Basic Servo

nets:
  N1: Part1.PWRIN, S1.L1
  GND: Part1.GND, J1.gnd, J2.gnd, J3.gnd, J5.gnd, M1.Pin_2, J4.gnd
  N2: Part1.VCC, M1.Pin_1
  N3: A1.Pin_1, M1.Pin_3
  N4: A1.Pin_14, A1.Pin_32, M1.Pin_4
  N5: S1.COM, JACK1.POS

notes:
  Adjust to 3.3V for the ESP32
  Hand/Gripper
  Wrist
  Elbow
  Shoulder
  Base

custom parts:
  16-Channel 12-bit PWM Servo Driver - I2C: You want to make a cool robot, maybe a hexapod walker, or maybe just a piece of art with a lot of moving parts. Or maybe you want to drive a lot of LEDs with precise PWM output. Using only two pins, control 16 free-running PWM outputs! You can even chain up 62 breakouts to control up to 992 PWM outputs.
  ESP32 DevKitc V4: ESP32-DevKitC board with ESP32-WROOM-32 module. ESP32-DevKitC V4 is a small-sized ESP32-based development board produced by Espressif. Most of the pins on the ESP module are broken out to the pin headers on the board. The pins D0, D1, D2, D3, CMD and CLK are used internally for communication between ESP32 and SPI flash memory. They are grouped on both sides near the USB connector. Avoid using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
